# Fritzing sketch TEAM 14 AR13,AR27 (saved by Fritzing 0.9.3b)
breadboards: 1

parts:
  R1 = Resistor [tolerance=±5% resistance=220 package=THT]
  R2 = Photocell (LDR) [package=THT]
  부품1 = Arduino Uno (Rev3)
  S1 = Pushbutton [package="[SMD]"]
  U1 = LCD-16X2 [package=lcd-16x2_noholes]
  M1 = Stepper Motor - Unipolar

nets:
  N1: R1.Pin_0, R2.pin_0
  GND: R1.Pin_1, 부품1.GND, U1.VSS
  N2: R2.pin_1, 부품1.A0
  N3: 부품1.A4/SDA, U1.VO
  N4: 부품1.A5/SCL, U1.RS, U1.R_W
  N5: 부품1.D8, M1.B
  N6: 부품1.D9_PWM, M1.C
  N7: 부품1.D10_PWM/SS, M1.COMMON_1
  N8: 부품1.D11_PWM/MOSI, M1.A
  N9: 부품1.D2, S1.Pin_3, S1.Pin_4
  5V: 부품1.5V, S1.Pin_1, S1.Pin_2, U1.VDD
