# Fritzing sketch ar13_4led (saved by Fritzing 0.9.3b)
breadboards: 1

parts:
  부품1 = Arduino Uno (Rev3)
  R1 = Resistor [tolerance=±5% resistance=330 package=THT]
  LED1 = LED - 5mm [color="Orange (620nm)" package="5 mm [THT]"]
  LED2 = LED - 5mm [color="Yellow (574nm)" package="5 mm [THT]"]
  LED3 = LED - 5mm [color="Blue (525nm)" package="5 mm [THT]"]
  LED4 = LED - 5mm [color="Red (633nm)" package="5 mm [THT]"]
  R3 = Resistor [tolerance=±5% resistance=330 package=THT]
  R4 = Resistor [tolerance=±5% resistance=330 package=THT]
  R5 = Resistor [tolerance=±5% resistance=330 package=THT]

nets:
  N1: 부품1.D9_PWM, LED1.anode
  N2: 부품1.D3_PWM, LED3.anode
  N3: 부품1.D5_PWM, LED2.anode
  N4: 부품1.D6_PWM, LED4.anode
  N5: 부품1.GND, R1.Pin_0, R3.Pin_0, R4.Pin_0, R5.Pin_0
  N6: R1.Pin_1, LED3.cathode
  N7: LED1.cathode, R5.Pin_1
  N8: LED2.cathode, R3.Pin_1
  N9: LED4.cathode, R4.Pin_1
