# Fritzing sketch ar13_RGB (saved by Fritzing 0.9.3b)
breadboards: 1

parts:
  부품1 = Arduino Uno (Rev3)
  R3 = Resistor [tolerance=±5% resistance=330 package=THT]
  R4 = Resistor [tolerance=±5% resistance=330 package=THT]
  R5 = Resistor [tolerance=±5% resistance=330 package=THT]
  LED5 = RGB LED (com. cathode, rgb) [package="5 mm [THT]"]

nets:
  N1: 부품1.GND, LED5.common_cathode
  N2: 부품1.D3_PWM, R5.Pin_0
  N3: 부품1.D5_PWM, R3.Pin_0
  N4: 부품1.D6_PWM, R4.Pin_0
  N5: R3.Pin_1, LED5.green_anode
  N6: R4.Pin_1, LED5.blue_anode
  N7: R5.Pin_1, LED5.red_anode
